# Fritzing sketch Fritzing (saved by Fritzing 0.9.4)
breadboards: 1

parts:
  M1 = RioRand LM2596
  Capacitive_Soil_Moisture_Sensor1 = DFRobot Capacitive Soil Moisture Sensor V1.0 [part_number=SEN0193]
  Part1 = Adafruit AHT20 Temperature and Humidity Sensor [part_number="Adafruit #4566"]
  HLK-PM1 = HLK-PM01
  WeMos_D1_Mini1 = WeMos D1 Mini

nets:
  N1: M1.Pin_1, HLK-PM1.+Vo
  N2: M1.Pin_2, HLK-PM1.-Vo
  VCC: M1.Pin_3, Capacitive_Soil_Moisture_Sensor1.VCC, Part1.VCC, WeMos_D1_Mini1.3V3
  GND: M1.Pin_4, Capacitive_Soil_Moisture_Sensor1.GND, Part1.GND, WeMos_D1_Mini1.G
  N3: Capacitive_Soil_Moisture_Sensor1.A, WeMos_D1_Mini1.A0
  N4: Part1.SDA, WeMos_D1_Mini1.D2
  N5: Part1.SCL, WeMos_D1_Mini1.D1

custom parts:
  DFRobot Capacitive Soil Moisture Sensor V1.0: DFRobot Capacitive Soil Moisture Sensor V1.0 This product measures soil moisture levels by capacitive sensing, rather than resistive sensing like other types of moisture sensor. It is made of a corrosion resistant material giving it a long service life. Insert it into soil and impress your friends with the real-time soil moisture data! The product includes an on-board voltage regulator which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
  Adafruit AHT20 Temperature and Humidity Sensor: The AHT20 is a nice but inexpensive temperature and humidity sensor from the same folks that brought us the DHT22. You can take sensor readings as often as you like, and it uses standard I2C so its super easy to use with any Arduino or Linux/Raspberry Pi board. This sensor has a typical accuracy of +- 2% relative humidity, and +-0.3 °C. There is only one I2C address so its not a good option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
